# Fritzing sketch traffic-light-controller (saved by Fritzing 0.9.3b)
circuit board: 10.499cm x 6.06918cm

parts:
  IC1 = ULN2803A [part_number=ULN2803A package=THT]
  U1 = Sharp PC847X [part_number=TLP521-4 package=THT]
  R1 = Resistor [tolerance=±5% resistance=100 package=THT]
  R2 = Resistor [tolerance=±5% resistance=100 package=THT]
  R8 = Resistor [tolerance=±5% resistance=100 package=THT]
  R7 = Resistor [tolerance=±5% resistance=100 package=THT]
  R6 = Resistor [tolerance=±5% resistance=100 package=THT]
  R5 = Resistor [tolerance=±5% resistance=100 package=THT]
  R4 = Resistor [tolerance=±5% resistance=100 package=THT]
  R3 = Resistor [tolerance=±5% resistance=100 package=THT]
  U2 = Sharp PC847X [part_number=TLP521-4 package=THT]
  J6 = Camdenboss CTB0158-12 [part_number=CTB0158-12 package=THT]
  J5 = Camdenboss CTB0158-2 [part_number=CTB0158-2 package=THT]
  J7 = Camdenboss CTB0158-12 [part_number=CTB0158-12 package=THT]
  J10 = shrouded pin header, 40 pins [form="♂ (shrouded male)"]
  LED1 = LED - 5mm [color="Green (555nm)" package="5 mm [THT]"]
  LED2 = LED - 5mm [color="Red (633nm)" package="5 mm [THT]"]
  LED3 = LED - 5mm [color="Green (555nm)" package="5 mm [THT]"]
  LED4 = LED - 5mm [color="Red (633nm)" package="5 mm [THT]"]
  LED5 = LED - 5mm [color="Green (555nm)" package="5 mm [THT]"]
  LED6 = LED - 5mm [color="Red (633nm)" package="5 mm [THT]"]
  LED7 = LED - 5mm [color="Green (555nm)" package="5 mm [THT]"]
  LED8 = LED - 5mm [color="Red (633nm)" package="5 mm [THT]"]
  J3 = Camdenboss CTB0158-2 [part_number=CTB0158-2 package=THT]
  12V_C+ = Power plug
  LED9 = LED - 5mm [color="Green (555nm)" package="5 mm [THT]"]
  LED10 = LED - 5mm [color="Green (555nm)" package="5 mm [THT]"]
  LED11 = LED - 5mm [color="Green (555nm)" package="5 mm [THT]"]
  LED12 = LED - 5mm [color="Green (555nm)" package="5 mm [THT]"]
  LED13 = LED - 5mm [color="Red (633nm)" package="5 mm [THT]"]
  LED14 = LED - 5mm [color="Red (633nm)" package="5 mm [THT]"]
  LED15 = LED - 5mm [color="Red (633nm)" package="5 mm [THT]"]
  LED16 = LED - 5mm [color="Red (633nm)" package="5 mm [THT]"]
  IC2 = ULN2803A [part_number=ULN2803A package=THT]
  U3 = Sharp PC847X [part_number=TLP521-4 package=THT]
  U4 = Sharp PC847X [part_number=TLP521-4 package=THT]
  R9 = Resistor [tolerance=±5% resistance=100 package=THT]
  R10 = Resistor [tolerance=±5% resistance=100 package=THT]
  R11 = Resistor [tolerance=±5% resistance=100 package=THT]
  R12 = Resistor [tolerance=±5% resistance=100 package=THT]
  R13 = Resistor [tolerance=±5% resistance=100 package=THT]
  R14 = Resistor [tolerance=±5% resistance=100 package=THT]
  R15 = Resistor [tolerance=±5% resistance=100 package=THT]
  R16 = Resistor [tolerance=±5% resistance=100 package=THT]
  LED17 = LED - 5mm [color="Green (555nm)" package="5 mm [THT]"]
  LED18 = LED - 5mm [color="Green (555nm)" package="5 mm [THT]"]
  LED19 = LED - 5mm [color="Green (555nm)" package="5 mm [THT]"]
  LED20 = LED - 5mm [color="Green (555nm)" package="5 mm [THT]"]
  LED21 = LED - 5mm [color="Red (633nm)" package="5 mm [THT]"]
  LED22 = LED - 5mm [color="Red (633nm)" package="5 mm [THT]"]
  LED23 = LED - 5mm [color="Red (633nm)" package="5 mm [THT]"]
  LED24 = LED - 5mm [color="Red (633nm)" package="5 mm [THT]"]
  IC3 = ULN2803A [part_number=ULN2803A package=THT]
  U5 = Sharp PC847X [part_number=TLP521-4 package=THT]
  U6 = Sharp PC847X [part_number=TLP521-4 package=THT]
  R17 = Resistor [tolerance=±5% resistance=100 package=THT]
  R18 = Resistor [tolerance=±5% resistance=100 package=THT]
  R19 = Resistor [tolerance=±5% resistance=100 package=THT]
  R20 = Resistor [tolerance=±5% resistance=100 package=THT]
  R21 = Resistor [tolerance=±5% resistance=100 package=THT]
  R22 = Resistor [tolerance=±5% resistance=100 package=THT]
  R23 = Resistor [tolerance=±5% resistance=100 package=THT]
  R24 = Resistor [tolerance=±5% resistance=100 package=THT]
  J11 = Camdenboss CTB0158-12 [part_number=CTB0158-12 package=THT]
  J12 = Camdenboss CTB0158-12 [part_number=CTB0158-12 package=THT]  # not connected

nets:
  N1: IC1.In_1, J10.pin3
  N2: IC1.In_2, J10.pin5
  N3: IC1.In_3, J10.pin7
  N4: IC1.In_4, J10.pin11
  N5: IC1.In_5, J10.pin13
  N6: IC1.In_6, J10.pin15
  GND: IC1.0V, J10.pin9, J10.pin14, J10.pin20, J3.pin2
  N7: IC1.Out_8, R8.Pin_0
  N8: IC1.Out_7, R7.Pin_0
  N9: IC1.Out_6, R6.Pin_0
  N10: IC1.Out_5, R5.Pin_0
  N11: IC1.Out_4, R4.Pin_0
  N12: IC1.Out_3, R3.Pin_0
  N13: IC1.Out_2, R2.Pin_0
  N14: IC1.Out_1, R1.Pin_0
  5V: U1.Pin_1, U1.Pin_3, U1.Pin_5, U1.Pin_7, U2.Pin_1, U2.Pin_3, U2.Pin_5, U2.Pin_7, J3.pin1, U3.Pin_1, U3.Pin_3, U3.Pin_5, U3.Pin_7, U4.Pin_1, U4.Pin_3, U4.Pin_5, U4.Pin_7, U5.Pin_1, U5.Pin_3, U5.Pin_5, U5.Pin_7, U6.Pin_1, U6.Pin_3, U6.Pin_5, U6.Pin_7
  N15: U1.Pin_2, LED1.anode
  N16: U1.Pin_4, LED2.anode
  N17: U1.Pin_6, LED3.anode
  N18: U1.Pin_8, LED4.anode
  0.12V: U1.Pin_9, U1.Pin_11, U1.Pin_13, U1.Pin_15, U2.Pin_9, U2.Pin_11, U2.Pin_13, U2.Pin_15, J5.pin2, 12V_C+.GND, U3.Pin_9, U3.Pin_11, U3.Pin_13, U3.Pin_15, U4.Pin_9, U4.Pin_11, U4.Pin_13, U4.Pin_15, U5.Pin_9, U5.Pin_11, U5.Pin_13, U5.Pin_15, U6.Pin_9, U6.Pin_11, U6.Pin_13, U6.Pin_15
  N19: U1.Pin_10, J6.pin4
  N20: U1.Pin_12, J6.pin3
  N21: U1.Pin_14, J6.pin2
  N22: U1.Pin_16, J6.pin1
  N23: R1.Pin_1, LED1.cathode
  N24: R2.Pin_1, LED2.cathode
  N25: R8.Pin_1, LED8.cathode
  N26: R7.Pin_1, LED7.cathode
  N27: R6.Pin_1, LED6.cathode
  N28: R5.Pin_1, LED5.cathode
  N29: R4.Pin_1, LED4.cathode
  N30: R3.Pin_1, LED3.cathode
  N31: U2.Pin_2, LED5.anode
  N32: U2.Pin_4, LED6.anode
  N33: U2.Pin_6, LED7.anode
  N34: U2.Pin_8, LED8.anode
  N35: U2.Pin_10, J6.pin8
  N36: U2.Pin_12, J6.pin7
  N37: U2.Pin_14, J6.pin6
  N38: U2.Pin_16, J6.pin5
  N39: J6.pin9, U4.Pin_16
  N40: J6.pin10, U4.Pin_14
  N41: J6.pin11, U4.Pin_12
  N42: J6.pin12, U4.Pin_10
  12V: J5.pin1, J7.pin1, J7.pin2, J7.pin3, J7.pin4, J7.pin5, J7.pin6, J7.pin7, J7.pin8, J7.pin9, J7.pin10, J7.pin11, J7.pin12, 12V_C+.VCC
  N43: LED9.cathode, R13.Pin_1
  N44: LED9.anode, U3.Pin_6
  N45: LED10.cathode, R11.Pin_1
  N46: LED10.anode, U3.Pin_2
  N47: LED11.cathode, R9.Pin_1
  N48: LED11.anode, U4.Pin_6
  N49: LED12.cathode, R16.Pin_1
  N50: LED12.anode, U4.Pin_2
  N51: LED13.cathode, R14.Pin_1
  N52: LED13.anode, U3.Pin_8
  N53: LED14.cathode, R12.Pin_1
  N54: LED14.anode, U3.Pin_4
  N55: LED15.cathode, R10.Pin_1
  N56: LED15.anode, U4.Pin_8
  N57: LED16.cathode, R15.Pin_1
  N58: LED16.anode, U4.Pin_4
  N59: IC2.Out_8, R14.Pin_0
  N60: IC2.Out_7, R13.Pin_0
  N61: IC2.Out_6, R12.Pin_0
  N62: IC2.Out_5, R11.Pin_0
  N63: IC2.Out_4, R10.Pin_0
  N64: IC2.Out_3, R9.Pin_0
  N65: IC2.Out_2, R15.Pin_0
  N66: IC2.Out_1, R16.Pin_0
  N67: U3.Pin_10, J11.pin4
  N68: U3.Pin_12, J11.pin3
  N69: U3.Pin_14, J11.pin2
  N70: U3.Pin_16, J11.pin1
  N71: LED17.cathode, R21.Pin_1
  N72: LED17.anode, U5.Pin_6
  N73: LED18.cathode, R19.Pin_1
  N74: LED18.anode, U5.Pin_2
  N75: LED19.cathode, R17.Pin_1
  N76: LED19.anode, U6.Pin_6
  N77: LED20.cathode, R24.Pin_1
  N78: LED20.anode, U6.Pin_2
  N79: LED21.cathode, R22.Pin_1
  N80: LED21.anode, U5.Pin_8
  N81: LED22.cathode, R20.Pin_1
  N82: LED22.anode, U5.Pin_4
  N83: LED23.cathode, R18.Pin_1
  N84: LED23.anode, U6.Pin_8
  N85: LED24.cathode, R23.Pin_1
  N86: LED24.anode, U6.Pin_4
  N87: IC3.Out_8, R22.Pin_0
  N88: IC3.Out_7, R21.Pin_0
  N89: IC3.Out_6, R20.Pin_0
  N90: IC3.Out_5, R19.Pin_0
  N91: IC3.Out_4, R18.Pin_0
  N92: IC3.Out_3, R17.Pin_0
  N93: IC3.Out_2, R23.Pin_0
  N94: IC3.Out_1, R24.Pin_0
  N95: U5.Pin_10, J11.pin12
  N96: U5.Pin_12, J11.pin11
  N97: U5.Pin_14, J11.pin10
  N98: U5.Pin_16, J11.pin9
  N99: U6.Pin_10, J11.pin8
  N100: U6.Pin_12, J11.pin7
  N101: U6.Pin_14, J11.pin6
  N102: U6.Pin_16, J11.pin5

notes:
  0V
  12V
  5V
  Lamps
  RPi GPIO
  Granta
  Traffic
  Lights
